# Fritzing sketch Knocker_Fridger-WemosD1-v100 (saved by Fritzing 0.9.3b)
circuit board: 2.60848cm x 2.41574cm
circuit board: 3.57988cm x 3.54697cm
breadboards: 1

parts:
  WeMos_D1_Mini1 = WeMos D1 Mini
  VÄRME = RELAY [part_number=Värme package=relay-jzc]
  KYLA = RELAY [part_number=Kylskåp package=relay-jzc]
  Yellow = LED - 3mm [color="Green (570nm)" package="3 mm [THT]"]
  Green = LED - 3mm [color="Yellow (574nm)" package="3 mm [THT]"]
  150Ω = Resistor [tolerance=±5% resistance=150 package=THT]
  150Ω_2 = Resistor [tolerance=±5% resistance=150 package=THT]
  DHT22 = female pin header, 3 pins [form="♀ (female)"]

nets:
  N1: WeMos_D1_Mini1.5V, DHT22.pin3
  N2: WeMos_D1_Mini1.D2, 150Ω.Pin_1
  N3: WeMos_D1_Mini1.D3, 150Ω_2.Pin_1
  N4: WeMos_D1_Mini1.D5, DHT22.pin2
  N5: WeMos_D1_Mini1.D6, VÄRME.COIL1
  N6: WeMos_D1_Mini1.D7, KYLA.COIL1
  N7: WeMos_D1_Mini1.G, VÄRME.MAIN, KYLA.MAIN, Yellow.cathode, Green.cathode, DHT22.pin1
  N8: Yellow.anode, 150Ω.Pin_0
  N9: Green.anode, 150Ω_2.Pin_0

notes:
  +   -
